# Fritzing sketch schematic (saved by Fritzing 0.9.8b)

parts:
  ESP8266-12E_MCU = NodeMCU V1.0
  28BYJ-48_Stepper = 28BYJ-48 Stepper Motor
  ULN2003_Stepper_Driver = X113647 Stepper Driver Board [package=board]
  MP1584_DC-DC_Buck_Converter = LM2596 step down module
  12V-DC_Power = Power plug

nets:
  N1: ESP8266-12E_MCU.D0, ULN2003_Stepper_Driver.IN4
  N2: ESP8266-12E_MCU.D5, ULN2003_Stepper_Driver.IN1
  N3: ESP8266-12E_MCU.D6, ULN2003_Stepper_Driver.IN2
  N4: ESP8266-12E_MCU.D7, ULN2003_Stepper_Driver.IN3
  GND: ESP8266-12E_MCU.GND, ULN2003_Stepper_Driver.GND, MP1584_DC-DC_Buck_Converter.IN-, MP1584_DC-DC_Buck_Converter.OUT-, 12V-DC_Power.GND
  N5: ESP8266-12E_MCU.Vin, MP1584_DC-DC_Buck_Converter.OUT+
  N6: 28BYJ-48_Stepper.BLUE, ULN2003_Stepper_Driver.BLUE
  N7: 28BYJ-48_Stepper.PINK, ULN2003_Stepper_Driver.PINK
  N8: 28BYJ-48_Stepper.RED, ULN2003_Stepper_Driver.YELLOW
  N9: 28BYJ-48_Stepper.ORANGE, ULN2003_Stepper_Driver.ORANGE
  N10: 28BYJ-48_Stepper.YELLOW, ULN2003_Stepper_Driver.RED
  N11: ULN2003_Stepper_Driver.+V, MP1584_DC-DC_Buck_Converter.IN+, 12V-DC_Power.VCC

notes:
  12V  -->  3.4V

custom parts:
  NodeMCU V1.0: ESP8266 based NodeMCU
  28BYJ-48 Stepper Motor: 28BYJ-48 gear-reduction stepper motor (small)
  X113647 Stepper Driver Board: A common stepper motor driver board based on ULN2003APG darlington array
  LM2596 step down module: LM2596 DC-DC step down power supply module 3 A.
